// Logisim project homework2.circ as structural Verilog: 17 circuits, main circuit main
module main (
  input  Clock_Source,
  input  [15:0] in_2,
  input  in_3,
  input  [15:0] in_4
);

  wire button_1_out, Clk, clock_1_out;
  wire [15:0] bird_1_data_out, bird_1_timer_out;

  Clock clock_1 (.out(clock_1_out));
  Button button_1 (.out(button_1_out));
  Multiplexer #(.disabled(0), .enable("false")) multiplexer_1 (
    .in0(clock_1_out), .in1(button_1_out), .out(Clk), .sel(Clock_Source));
  LED led_1 (.in(Clk));
  Hex_Digit_Display hex_digit_display_1 (.value(bird_1_timer_out[15:12]), .dp(1'b0));
  bird bird_1 (
    ._16_bit_Pin_1(in_2), ._16_bit_Pin_2(in_4), .Push_Button_1(in_3), .Data_out(bird_1_data_out),
    .Clock(Clk), .Timer_out(bird_1_timer_out));
  Hex_Digit_Display hex_digit_display_2 (.value(bird_1_data_out[15:12]), .dp(1'b0));
  Hex_Digit_Display hex_digit_display_3 (.value(bird_1_timer_out[7:4]), .dp(1'b0));
  Hex_Digit_Display hex_digit_display_4 (.value(bird_1_timer_out[11:8]), .dp(1'b0));
  Hex_Digit_Display hex_digit_display_5 (.value(bird_1_data_out[11:8]), .dp(1'b0));
  Hex_Digit_Display hex_digit_display_6 (.value(bird_1_data_out[7:4]), .dp(1'b0));
  Hex_Digit_Display hex_digit_display_7 (.value(bird_1_timer_out[3:0]), .dp(1'b0));
  Hex_Digit_Display hex_digit_display_8 (.value(bird_1_data_out[3:0]), .dp(1'b0));

  // Notes on the sheet:
  //   Timer
  //   Data Out
endmodule

module bird (
  input  Clock,
  input  Push_Button_1,
  input  [15:0] _16_bit_Pin_1,
  input  [15:0] _16_bit_Pin_2,
  output [15:0] Data_out,
  output [15:0] Timer_out
);

  wire and_1_out, and_3_out, and_4_out, and_5_out, and_6_out, and_7_out, CLI, Clk, comparator_1_eq,
       comparator_2_eq, comparator_3_eq, comparator_4_eq, F_LD, IFlag, INT, INT_ACK, INT_LD, IO_LD, IO_MUX,
       IR_LD, MEM_LD, multiplexer_3_out, PC_INC, PC_LD, PC_MUX, REG_LD, REG_MUX, SP_minus_minus,
       SP_plus_plus, STI, Timer, Zero, ZF, ZF_LD;
  wire [1:0] ARMUX, DATA_MUX;
  wire [2:0] IO_ADDRESS;
  wire [11:0] IR_OUT;
  wire [15:0] adder_1_out, adder_2_out, AddrOut, ALU_RES, bit_extender_1_out, bit_extender_2_out,
       bit_extender_3_out, Din, Flags, INT_ADDR, IO_INPUT, multiplexer_1_out, multiplexer_8_out, PC, R1, R2,
       R3, R4, R5, R6, R7, ram_1_data, REG_DATA, SP, SRC_1, SRC_2, Time, Vector;

  Comparator #(.width(16), .mode("unsigned")) comparator_1 (
    .a(16'h34), .b(AddrOut), .eq(comparator_1_eq));  // open: gt, lt
  Multiplexer #(.select(2), .width(16), .enable("false")) multiplexer_1 (
    .in0(SRC_1), .in1(PC), .in2(Flags), .out(multiplexer_1_out), .sel(DATA_MUX));  // open: in3
  Multiplexer #(.disabled(0), .enable("false")) multiplexer_2 (
    .in0(Clock), .in1(1'b0), .out(Clk), .sel(multiplexer_3_out));
  Multiplexer #(.disabled(0), .enable("false")) multiplexer_3 (
    .in0(comparator_1_eq), .in1(1'b0), .out(multiplexer_3_out), .sel(1'b1));
  control_unit control_unit_1 (
    .IR_15_12(Din[15:12]), .PCINC(PC_INC), .PCLD(PC_LD), .SP_minus_minus(SP_minus_minus),
    .SP_plus_plus(SP_plus_plus), .PC_MUX(PC_MUX), .DATA_MUX(DATA_MUX), .ZF(ZF), .Clk(Clk), .ARMUX(ARMUX),
    .REGLD(REG_LD), .ZFLD(ZF_LD), .REG_MUX(REG_MUX), .MEMLD(MEM_LD), .IRLD(IR_LD), .IFlag(IFlag),
    .F_LD(F_LD), .INT_ACK(INT_ACK), .CLI(CLI), .SLI(STI), .INT(INT), .INT_LD(INT_LD));
  Multiplexer #(.select(3), .width(16), .enable("false")) multiplexer_4 (
    .in0(R1), .in1(R2), .in2(R3), .in3(R4), .in4(R5), .in5(R6), .in6(R7), .in7(SP), .out(SRC_1),
    .sel(IR_OUT[8:6]));
  assign bit_extender_1_out = {{15{1'b0}}, Push_Button_1};  // Bit_Extender bit_extender_1
  and and_1 (and_1_out, ~IO_MUX, MEM_LD);  // AND_Gate
  alu in1_in2 (.i1(SRC_1), .i2(SRC_2), .Result(ALU_RES), .Zero(Zero), .ALUOP(IR_OUT[11:6]));
  Multiplexer #(.select(3), .width(16), .enable("false")) multiplexer_5 (
    .in0(R1), .in1(R2), .in2(R3), .in3(R4), .in4(R5), .in5(R6), .in6(R7), .in7(SP), .out(SRC_2),
    .sel(IR_OUT[5:3]));
  RAM #(.addrWidth(16), .dataWidth(16), .bus("separate")) ram_1 (
    .addr(AddrOut), .din(multiplexer_1_out), .data(ram_1_data), .str(and_1_out), .sel(1'b1), .clk(Clk),
    .ld(1'b1));  // open: clr
  Multiplexer #(.select(3), .width(16), .disabled(0), .enable("false")) multiplexer_6 (
    .in0(bit_extender_1_out), .in1(_16_bit_Pin_1), .in2(_16_bit_Pin_2), .in4(Time), .out(IO_INPUT),
    .sel(IO_ADDRESS));  // open: in3, in5, in6, in7
  assign bit_extender_2_out = {{4{IR_OUT[11]}}, IR_OUT};  // Bit_Extender bit_extender_2
  Multiplexer #(.select(2), .width(16), .disabled(0), .enable("false")) multiplexer_7 (
    .in0(ram_1_data), .in1(IO_INPUT), .in2(Vector), .out(Din), .sel({INT_ACK, IO_MUX}));  // open: in3
  Adder #(.width(16)) adder_1 (.a(PC), .b(bit_extender_2_out), .out(adder_1_out));  // open: cin, cout
  Multiplexer #(.width(16), .enable("false")) multiplexer_8 (
    .in0(adder_1_out), .in1(Din), .out(multiplexer_8_out), .sel(PC_MUX));
  Comparator #(.width(3), .mode("unsigned")) comparator_2 (
    .a(3'b110), .b(IO_ADDRESS), .eq(comparator_2_eq));  // open: gt, lt
  and and_2 (IO_LD, IO_MUX, MEM_LD);
  and and_3 (and_3_out, IO_LD, comparator_3_eq);
  Comparator #(.width(3), .mode("unsigned")) comparator_3 (
    .a(3'b011), .b(IO_ADDRESS), .eq(comparator_3_eq));  // open: gt, lt
  and and_4 (and_4_out, IO_LD, comparator_4_eq);
  Comparator #(.width(3), .mode("unsigned")) comparator_4 (
    .a(3'b101), .b(IO_ADDRESS), .eq(comparator_4_eq));  // open: gt, lt
  Multiplexer #(.width(16), .enable("false")) multiplexer_9 (.in0(ALU_RES), .in1(Din), .out(REG_DATA), .sel(REG_MUX));
  and and_5 (and_5_out, IO_LD, comparator_2_eq);
  pic pic_1 (
    .Mask(SRC_1), .Hector(Vector), .INT(INT), .IRQ1(Timer), .Clk(Clk), .MaskLD(and_5_out));  // open: IRQ2, IRQ3, IRQ4
  register_16 register_16_1 (.Data(SRC_1), .Load(and_3_out), .Q(Data_out), .Clk(Clk));
  register_16 register_16_2 (.Data(SRC_1), .Load(and_4_out), .Q(Timer_out), .Clk(Clk));
  PC pc_1 (.Data(multiplexer_8_out), .Load(PC_LD), .Clk(Clk), .Increment(PC_INC), .out_5(PC));
  assign bit_extender_3_out = {{13{1'b0}}, Din[2:0]};  // Bit_Extender bit_extender_3
  instruction_register instruction_register_1 (.in_1(Din[11:0]), .IR_LD(IR_LD), .Clk(Clk), .IR(IR_OUT));
  Adder #(.width(16)) adder_2 (.a(16'he000), .b(bit_extender_3_out), .out(adder_2_out));  // open: cin, cout
  Multiplexer #(.select(2), .width(16), .enable("false")) multiplexer_10 (
    .in0(PC), .in1(SRC_2), .in2(SP), .in3(INT_ADDR), .out(AddrOut), .sel(ARMUX));
  register_16 register_16_3 (.Data(adder_2_out), .Load(INT_LD), .Q(INT_ADDR), .Clk(Clk));
  // Probe on 16'h400
  register_bank register_bank_1 (
    .Data(REG_DATA), .Register_Select(IR_OUT[2:0]), .REG_LD(REG_LD), .Dout1(R1), .Dout2(R2), .Dout3(R3),
    .Dout4(R4), .Dout5(R5), .Dout6(R6), .Flags(Flags), .SP(SP), .Clk(Clk), .SP_minus_minus(SP_minus_minus),
    .SP_plus_plus(SP_plus_plus), .ZFLD(ZF_LD), .IF_SET(STI), .IF_RESET(CLI), .F_LD(F_LD), .Zero(Zero),
    .IF(IFlag), .ZF(ZF));
  and and_6 (and_6_out, and_7_out, IO_MUX);
  timer timer_1 (.TimerInterrupt(Timer), .Clk(Clk), .Tick_Frequency(16'h400), .Time(Time), .TimeRead(and_6_out));
  // Probe on Time
  Bit_Extender #(.in_width(16), .out_width(3)) bit_extender_4 (.in(AddrOut), .out(IO_ADDRESS));
  and and_7 (and_7_out, ~IO_ADDRESS[0], ~IO_ADDRESS[1], IO_ADDRESS[2]);  // AND_Gate
  and and_8 (IO_MUX, AddrOut[12], ~AddrOut[13], AddrOut[14], AddrOut[15]);  // AND_Gate

  // Other names for the same wires on the sheet: IR_IN[11:0] = Din[11:0]; Opcode[3:0] = Din[15:12];
  //   IR_OUT_2_0[2:0] = IR_OUT[2:0]; IR_OUT_5_3[2:0] = IR_OUT[5:3]; IR_OUT_8_6[2:0] = IR_OUT[8:6];
  //   IR_OUT_11_6[5:0] = IR_OUT[11:6]

  // Notes on the sheet:
  //   Table address
  //   TempReg
endmodule

module driver (
  input  [3:0] Qin,
  input  Pin,
  output a,
  output b,
  output p,
  output c,
  output d,
  output e,
  output f,
  output g
);

  wire and_1_out, and_2_out, and_3_out, and_4_out, and_5_out, and_6_out, and_7_out, and_8_out, and_9_out,
       and_10_out, and_11_out, and_12_out, and_13_out, and_14_out, and_15_out, and_16_out, not_1_out;

  and and_1 (and_1_out, ~Qin[0], ~Qin[2]);  // AND_Gate
  and and_2 (and_2_out, Qin[0], Qin[2]);
  and and_3 (and_3_out, Qin[1], Qin[0]);
  and and_4 (and_4_out, ~Qin[1], ~Qin[0]);  // AND_Gate
  and and_5 (and_5_out, ~Qin[2], ~Qin[0]);  // AND_Gate
  and and_6 (and_6_out, Qin[1], ~Qin[0]);  // AND_Gate
  and and_7 (and_7_out, ~Qin[2], Qin[1]);  // AND_Gate
  and and_8 (and_8_out, ~Qin[1], Qin[2], Qin[0]);  // AND_Gate
  and and_9 (and_9_out, ~Qin[2], ~Qin[0]);  // AND_Gate
  and and_10 (and_10_out, Qin[1], ~Qin[0]);  // AND_Gate
  and and_11 (and_11_out, ~Qin[1], ~Qin[0]);  // AND_Gate
  and and_12 (and_12_out, Qin[2], ~Qin[1]);  // AND_Gate
  and and_13 (and_13_out, Qin[2], ~Qin[0]);  // AND_Gate
  and and_14 (and_14_out, Qin[2], ~Qin[1]);  // AND_Gate
  and and_15 (and_15_out, ~Qin[2], Qin[1]);  // AND_Gate
  and and_16 (and_16_out, Qin[1], ~Qin[0]);  // AND_Gate
  or or_1 (a, and_1_out, and_2_out, Qin[1], Qin[3]);
  not not_1 (not_1_out, Qin[2]);
  or or_2 (b, not_1_out, and_3_out, and_4_out);
  or or_3 (c, Qin[2], Qin[0], ~Qin[1]);  // OR_Gate
  or or_4 (d, Qin[3], and_5_out, and_6_out, and_7_out, and_8_out);
  or or_5 (e, and_9_out, and_10_out);
  or or_6 (f, Qin[3], and_11_out, and_12_out, and_13_out);
  or or_7 (g, Qin[3], and_14_out, and_15_out, and_16_out);
  _7_Segment_Display u_7_segment_display_1 (.g(g), .f(f), .a(a), .b(b), .e(e), .d(d), .c(c), .dp(Pin));

  assign p = Pin;
endmodule

module register_1 (
  input  CLK,
  input  Data,
  input  Load,
  output Q
);

  wire and_1_out, and_2_out;

  and and_1 (and_1_out, Data, Load);
  and and_2 (and_2_out, ~Data, Load);  // AND_Gate
  S_R_Flip_Flop s_r_ff_1 (.S(and_1_out), .clk(CLK), .R(and_2_out), .Q(Q), .en(1'b1));  // open: Qn, preset, reset
endmodule

module register_4 (
  input  [3:0] Data,
  input  Load,
  input  Clk,
  output [3:0] Q
);

  register_1 register_1_1 (.CLK(Clk), .Data(Data[0]), .Load(Load), .Q(Q[0]));
  register_1 register_1_2 (.CLK(Clk), .Data(Data[1]), .Load(Load), .Q(Q[1]));
  register_1 register_1_3 (.CLK(Clk), .Data(Data[2]), .Load(Load), .Q(Q[2]));
  register_1 register_1_4 (.CLK(Clk), .Data(Data[3]), .Load(Load), .Q(Q[3]));
endmodule

module register_5 (
  input  [4:0] Data,
  input  in_2,
  input  Clk,
  output [4:0] Q
);

  register_1 register_1_1 (.CLK(Clk), .Data(Data[0]), .Load(in_2), .Q(Q[0]));
  register_1 register_1_2 (.CLK(Clk), .Data(Data[1]), .Load(in_2), .Q(Q[1]));
  register_1 register_1_3 (.CLK(Clk), .Data(Data[2]), .Load(in_2), .Q(Q[2]));
  register_1 register_1_4 (.CLK(Clk), .Data(Data[3]), .Load(in_2), .Q(Q[3]));
  register_1 register_1_5 (.CLK(Clk), .Data(Data[4]), .Load(in_2), .Q(Q[4]));

  // Other names for the same wires on the sheet: Load = in_2
endmodule

module register_12 (
  input  [11:0] Data,
  input  Load,
  input  Clk,
  output [11:0] Q
);

  register_1 register_1_1 (.CLK(Clk), .Data(Data[0]), .Load(Load), .Q(Q[0]));
  register_1 register_1_2 (.CLK(Clk), .Data(Data[1]), .Load(Load), .Q(Q[1]));
  register_1 register_1_3 (.CLK(Clk), .Data(Data[2]), .Load(Load), .Q(Q[2]));
  register_1 register_1_4 (.CLK(Clk), .Data(Data[3]), .Load(Load), .Q(Q[3]));
  register_1 register_1_5 (.CLK(Clk), .Data(Data[4]), .Load(Load), .Q(Q[4]));
  register_1 register_1_6 (.CLK(Clk), .Data(Data[5]), .Load(Load), .Q(Q[5]));
  register_1 register_1_7 (.CLK(Clk), .Data(Data[6]), .Load(Load), .Q(Q[6]));
  register_1 register_1_8 (.CLK(Clk), .Data(Data[7]), .Load(Load), .Q(Q[7]));
  register_1 register_1_9 (.CLK(Clk), .Data(Data[8]), .Load(Load), .Q(Q[8]));
  register_1 register_1_10 (.CLK(Clk), .Data(Data[9]), .Load(Load), .Q(Q[9]));
  register_1 register_1_11 (.CLK(Clk), .Data(Data[10]), .Load(Load), .Q(Q[10]));
  register_1 register_1_12 (.CLK(Clk), .Data(Data[11]), .Load(Load), .Q(Q[11]));
endmodule

module register_16 (
  input  [15:0] Data,
  input  Load,
  input  Clk,
  output [15:0] Q
);

  register_1 register_1_1 (.CLK(Clk), .Data(Data[0]), .Load(Load), .Q(Q[0]));
  register_1 register_1_2 (.CLK(Clk), .Data(Data[1]), .Load(Load), .Q(Q[1]));
  register_1 register_1_3 (.CLK(Clk), .Data(Data[2]), .Load(Load), .Q(Q[2]));
  register_1 register_1_4 (.CLK(Clk), .Data(Data[3]), .Load(Load), .Q(Q[3]));
  register_1 register_1_5 (.CLK(Clk), .Data(Data[4]), .Load(Load), .Q(Q[4]));
  register_1 register_1_6 (.CLK(Clk), .Data(Data[5]), .Load(Load), .Q(Q[5]));
  register_1 register_1_7 (.CLK(Clk), .Data(Data[6]), .Load(Load), .Q(Q[6]));
  register_1 register_1_8 (.CLK(Clk), .Data(Data[7]), .Load(Load), .Q(Q[7]));
  register_1 register_1_9 (.CLK(Clk), .Data(Data[8]), .Load(Load), .Q(Q[8]));
  register_1 register_1_10 (.CLK(Clk), .Data(Data[9]), .Load(Load), .Q(Q[9]));
  register_1 register_1_11 (.CLK(Clk), .Data(Data[10]), .Load(Load), .Q(Q[10]));
  register_1 register_1_12 (.CLK(Clk), .Data(Data[11]), .Load(Load), .Q(Q[11]));
  register_1 register_1_13 (.CLK(Clk), .Data(Data[12]), .Load(Load), .Q(Q[12]));
  register_1 register_1_14 (.CLK(Clk), .Data(Data[13]), .Load(Load), .Q(Q[13]));
  register_1 register_1_15 (.CLK(Clk), .Data(Data[14]), .Load(Load), .Q(Q[14]));
  register_1 register_1_16 (.CLK(Clk), .Data(Data[15]), .Load(Load), .Q(Q[15]));
endmodule

module register_incdec (
  input  [15:0] Data,
  input  Load,
  input  Clk,
  input  Increment,
  input  Decrement,
  output [15:0] out_6
);

  wire not_1_out, or_1_out, or_2_out;
  wire [15:0] adder_1_out, multiplexer_1_out, multiplexer_2_out, subtractor_1_out;

  or or_1 (or_1_out, Increment, Decrement);
  Multiplexer #(.width(16), .enable("false")) multiplexer_1 (
    .in0(multiplexer_2_out), .in1(Data), .out(multiplexer_1_out), .sel(not_1_out));
  or or_2 (or_2_out, Load, or_1_out);
  not not_1 (not_1_out, or_1_out);
  register_16 register_16_1 (.Data(multiplexer_1_out), .Load(or_2_out), .Q(out_6), .Clk(Clk));
  Adder #(.width(16)) adder_1 (.a(16'h1), .b(out_6), .out(adder_1_out));  // open: cin, cout
  Multiplexer #(.width(16), .enable("false")) multiplexer_2 (
    .in0(adder_1_out), .in1(subtractor_1_out), .out(multiplexer_2_out), .sel(Decrement));
  Subtractor #(.width(16)) subtractor_1 (.a(out_6), .b(16'h1), .out(subtractor_1_out));  // open: bin, bout
endmodule

module register_bank (
  input  [15:0] Data,
  input  [2:0] Register_Select,
  input  REG_LD,
  input  Clk,
  input  SP_plus_plus,
  input  Zero,
  input  SP_minus_minus,
  input  F_LD,
  input  ZFLD,
  input  IF_SET,
  input  IF_RESET,
  output [15:0] Dout1,
  output [15:0] Dout2,
  output [15:0] Dout3,
  output [15:0] Dout4,
  output [15:0] Dout5,
  output [15:0] Dout6,
  output [15:0] Flags,
  output [15:0] SP,
  output ZF,
  output IF
);

  wire and_1_out, and_2_out, and_3_out, and_4_out, and_5_out, and_6_out, and_7_out, and_8_out,
       decoder_1_out0, decoder_1_out1, decoder_1_out2, decoder_1_out3, decoder_1_out4, decoder_1_out5,
       multiplexer_1_out, or_1_out;

  Decoder #(.select(3), .enable("false")) decoder_1 (
    .out0(decoder_1_out0), .out1(decoder_1_out1), .out2(decoder_1_out2), .out3(decoder_1_out3),
    .out4(decoder_1_out4), .out5(decoder_1_out5), .sel(Register_Select));  // open: out6, out7
  and and_1 (and_1_out, decoder_1_out0, REG_LD);
  and and_2 (and_2_out, decoder_1_out1, REG_LD);
  and and_3 (and_3_out, decoder_1_out2, REG_LD);
  and and_4 (and_4_out, decoder_1_out3, REG_LD);
  and and_5 (and_5_out, decoder_1_out4, REG_LD);
  and and_6 (and_6_out, decoder_1_out5, REG_LD);
  register_16 register_16_1 (.Data(Data), .Load(and_1_out), .Q(Dout1), .Clk(Clk));
  register_16 register_16_2 (.Data(Data), .Load(and_2_out), .Q(Dout2), .Clk(Clk));
  register_16 register_16_3 (.Data(Data), .Load(and_3_out), .Q(Dout3), .Clk(Clk));
  register_16 register_16_4 (.Data(Data), .Load(and_4_out), .Q(Dout4), .Clk(Clk));
  register_16 register_16_5 (.Data(Data), .Load(and_5_out), .Q(Dout5), .Clk(Clk));
  register_16 register_16_6 (.Data(Data), .Load(and_6_out), .Q(Dout6), .Clk(Clk));
  stack_pointer stack_pointer_1 (.SP_plus_plus(SP_plus_plus), .SP_minus_minus(SP_minus_minus), .CLK(Clk), .out_4(SP));
  Multiplexer #(.disabled(0), .enable("false")) multiplexer_1 (
    .in0(Zero), .in1(Data[0]), .out(multiplexer_1_out), .sel(F_LD));
  or or_1 (or_1_out, F_LD, ZFLD);
  and and_7 (and_7_out, multiplexer_1_out, or_1_out);
  and and_8 (and_8_out, ~multiplexer_1_out, or_1_out);  // AND_Gate
  S_R_Flip_Flop s_r_ff_1 (.S(and_7_out), .clk(Clk), .R(and_8_out), .Q(ZF), .en(1'b1));  // open: Qn, preset, reset
  S_R_Flip_Flop s_r_ff_2 (.S(IF_SET), .clk(Clk), .R(IF_RESET), .Q(IF), .en(1'b1));  // open: Qn, preset, reset
  assign Flags = {{14{1'b0}}, {IF, ZF}};  // Bit_Extender bit_extender_1

  // Other names for the same wires on the sheet: Data_0 = Data[0]; Data_1 = Data[1]; FlagLD = F_LD
endmodule

module alu (
  input  [15:0] i1,
  input  [15:0] i2,
  input  [5:0] ALUOP,
  output [15:0] Result,
  output Zero
);

  wire [15:0] adder_1_out, adder_2_out, and_1_out, multiplexer_1_out, not_1_out, or_1_out, subtractor_1_out,
       subtractor_2_out, xor_1_out;

  Adder #(.width(16)) adder_1 (.a(i1), .b(i2), .out(adder_1_out));  // open: cin, cout
  Subtractor #(.width(16)) subtractor_1 (.a(i1), .b(i2), .out(subtractor_1_out));  // open: bin, bout
  assign and_1_out = i1 & i2;  // AND_Gate and_1, 16 bits wide
  assign or_1_out = i1 | i2;  // OR_Gate or_1, 16 bits wide
  assign xor_1_out = i1 ^ i2;  // XOR_Gate xor_1, 16 bits wide
  assign not_1_out = ~i2;  // NOT_Gate not_1, 16 bits wide
  Adder #(.width(16)) adder_2 (.a(i2), .b(16'h1), .out(adder_2_out));  // open: cin, cout
  Subtractor #(.width(16)) subtractor_2 (.a(i2), .b(16'h1), .out(subtractor_2_out));  // open: bin, bout
  Multiplexer #(.select(3), .width(16), .enable("false")) multiplexer_1 (
    .in0(not_1_out), .in1(i2), .in2(adder_2_out), .in3(subtractor_2_out), .in4({16{1'b0}}), .in5({16{1'b0}}),
    .in6({16{1'b0}}), .in7({16{1'b0}}), .out(multiplexer_1_out), .sel(ALUOP[2:0]));
  Multiplexer #(.select(3), .width(16), .enable("false")) multiplexer_2 (
    .in0(adder_1_out), .in1(subtractor_1_out), .in2(and_1_out), .in3(or_1_out), .in4(xor_1_out),
    .in5({16{1'b0}}), .in6({16{1'b0}}), .in7(multiplexer_1_out), .out(Result), .sel(ALUOP[5:3]));
  nor nor_1 (Zero, Result[15], Result[14], Result[13], Result[12], Result[11], Result[10], Result[9], Result[8], Result[7], Result[6], Result[5], Result[4], Result[3], Result[2], Result[1], Result[0]);
endmodule

module PC (
  input  [15:0] Data,
  input  Load,
  input  Clk,
  input  Increment,
  output [15:0] out_5
);

  wire not_1_out, or_1_out;
  wire [15:0] adder_1_out, multiplexer_1_out;

  Multiplexer #(.width(16), .enable("false")) multiplexer_1 (
    .in0(adder_1_out), .in1(Data), .out(multiplexer_1_out), .sel(not_1_out));
  or or_1 (or_1_out, Load, Increment);
  not not_1 (not_1_out, Increment);
  register_16 register_16_1 (.Data(multiplexer_1_out), .Load(or_1_out), .Q(out_5), .Clk(Clk));
  Adder #(.width(16)) adder_1 (.a(16'h1), .b(out_5), .out(adder_1_out));  // open: cin, cout
endmodule

module control_unit (
  input  [3:0] IR_15_12,
  input  ZF,
  input  Clk,
  input  INT,
  input  IFlag,
  output IRLD,
  output MEMLD,
  output REG_MUX,
  output ZFLD,
  output REGLD,
  output [1:0] ARMUX,
  output PCINC,
  output PCLD,
  output SP_minus_minus,
  output SP_plus_plus,
  output PC_MUX,
  output [1:0] DATA_MUX,
  output SLI,
  output CLI,
  output INT_LD,
  output INT_ACK,
  output F_LD
);

  wire and_2_out, and_3_out;
  wire [0:0] and_1_out;
  wire [3:0] multiplexer_1_out;
  wire [4:0] bit_extender_1_out, multiplexer_2_out, multiplexer_3_out, NEXT_ADDR, register_5_1_q;
  wire [24:24] rom_1_data;

  and and_1 (and_1_out[0], ~IR_15_12[0], ~IR_15_12[1], IR_15_12[2], ~IR_15_12[3]);  // AND_Gate
  Multiplexer #(.select(2), .width(4), .enable("false")) multiplexer_1 (
    .in0(IR_15_12), .in1(IR_15_12), .in2(IR_15_12), .in3(4'b0101), .out(multiplexer_1_out),
    .sel({ZF, and_1_out[0]}));
  assign bit_extender_1_out = {{1{1'b0}}, multiplexer_1_out};  // Bit_Extender bit_extender_1
  Multiplexer #(.width(5), .enable("false")) multiplexer_2 (
    .in0(NEXT_ADDR), .in1(bit_extender_1_out), .out(multiplexer_2_out), .sel(rom_1_data[24]));
  and and_2 (and_2_out, INT, IFlag, and_3_out);
  Multiplexer #(.width(5), .enable("false")) multiplexer_3 (
    .in0(multiplexer_2_out), .in1(5'b10011), .out(multiplexer_3_out), .sel(and_2_out));
  and and_3 (and_3_out, ~NEXT_ADDR[4], ~NEXT_ADDR[3], ~NEXT_ADDR[2], ~NEXT_ADDR[1], ~NEXT_ADDR[0]);  // AND_Gate
  register_5 register_5_1 (.Data(multiplexer_3_out), .in_2(1'b1), .Clk(Clk), .Q(register_5_1_q));
  ROM #(.addrWidth(5), .dataWidth(25)) rom_1 (
    .addr(register_5_1_q),
    .data({rom_1_data[24], F_LD, INT_ACK, INT_LD, CLI, SLI, DATA_MUX, PC_MUX, SP_plus_plus, SP_minus_minus, PCLD, PCINC, ARMUX, REGLD, ZFLD, REG_MUX, MEMLD, IRLD, NEXT_ADDR}),
    .sel(1'b1));

  // Notes on the sheet:
  //   contents of rom_1 (hex, n*v repeats v):
  //   100103f 1280 680 440 1000 12000 0 300 4840 8011 24845 8012 80000 100000 800f 808890 12800 a80 12880
  //   124854 644855 12c00
endmodule

module instruction_register (
  input  [11:0] in_1,
  input  IR_LD,
  input  Clk,
  output [11:0] IR
);

  register_12 register_12_1 (.Data(in_1), .Load(IR_LD), .Clk(Clk), .Q(IR));
endmodule

module stack_pointer (
  input  SP_plus_plus,
  input  SP_minus_minus,
  input  CLK,
  output [15:0] out_4
);

  wire or_1_out;

  or or_1 (or_1_out, SP_plus_plus, SP_minus_minus);
  register_incdec register_incdec_1 (
    .Data(out_4), .Load(or_1_out), .Clk(CLK), .Increment(SP_plus_plus), .Decrement(SP_minus_minus),
    .out_6(out_4));
endmodule

module pic (
  input  IRQ1,
  input  IRQ2,
  input  IRQ3,
  input  IRQ4,
  input  [15:0] Mask,
  input  MaskLD,
  input  Clk,
  output [15:0] Hector,
  output INT
);

  wire [3:0] priority_encoder_1_out;
  wire [15:0] and_1_out, register_16_1_q;

  register_16 register_16_1 (.Data(Mask), .Load(MaskLD), .Q(register_16_1_q), .Clk(Clk));
  assign and_1_out = {{12{1'b0}}, IRQ4, IRQ3, IRQ2, IRQ1} & ~register_16_1_q;  // AND_Gate and_1, 16 bits wide
  Priority_Encoder #(.select(4)) priority_encoder_1 (
    .in0(and_1_out[0]), .in1(and_1_out[1]), .in2(and_1_out[2]), .in3(and_1_out[3]), .in4(and_1_out[4]),
    .in5(and_1_out[5]), .in6(and_1_out[6]), .in7(and_1_out[7]), .in8(and_1_out[8]), .in9(and_1_out[9]),
    .in10(and_1_out[10]), .in11(and_1_out[11]), .in12(and_1_out[12]), .in13(and_1_out[13]),
    .in14(and_1_out[14]), .in15(and_1_out[15]), .out(priority_encoder_1_out), .gs(INT));  // open: en_out, en_in
  assign Hector = {{12{1'b0}}, priority_encoder_1_out};  // Bit_Extender bit_extender_1
endmodule

module timer (
  input  [15:0] Tick_Frequency,
  input  Clk,
  input  TimeRead,
  output TimerInterrupt,
  output [15:0] Time
);

  wire comparator_1_eq, comparator_1_lt, IntRegister, RegLD;
  wire [10:0] counter_1_q, Max_Value;
  wire [15:0] bit_extender_1_out, shifter_1_out, subtractor_1_out;

  Counter #(.width(11), .max('h7ff)) counter_1 (
    .count(1'b1), .Q(counter_1_q), .clk(Clk), .clr(comparator_1_lt));  // open: load, D, carry
  Comparator #(.width(11), .mode("unsigned")) comparator_1 (
    .a(Max_Value), .b(counter_1_q), .eq(comparator_1_eq), .lt(comparator_1_lt));  // open: gt
  Shifter #(.width(16), .shift("ar")) shifter_1 (.in(Tick_Frequency), .\dist (4'b0001), .out(shifter_1_out));
  assign bit_extender_1_out = {{12{1'b0}}, 4'b0001};  // Bit_Extender bit_extender_1
  Subtractor #(.width(16)) subtractor_1 (
    .a(shifter_1_out), .b(bit_extender_1_out), .out(subtractor_1_out));  // open: bin, bout
  register_1 register_1_1 (.CLK(Clk), .Data(comparator_1_eq), .Load(RegLD), .Q(IntRegister));
  Counter #(.width(16), .max('hffff)) counter_2 (
    .count(1'b1), .Q(Time), .clk(comparator_1_eq));  // open: load, D, carry, clr
  or or_1 (RegLD, ~IntRegister, TimeRead);  // OR_Gate
  Bit_Extender #(.in_width(16), .out_width(11)) bit_extender_2 (.in(subtractor_1_out), .out(Max_Value));
  or or_2 (TimerInterrupt, comparator_1_eq, IntRegister);
endmodule
